// Logisim project IT012_Lab01_25521955.circ as structural Verilog
module TN1 (
  input  A,
  input  B,
  input  C,
  output NotA,
  output andAB,
  output orAB,
  output nandAB,
  output norAB,
  output xorAB,
  output xnorAB,
  output xor3ABC,
  output nand3ABC,
  output CHAIN
);

  wire nand_3_out, xor_2_out;

  not not_1 (NotA, A);
  and and_1 (andAB, A, B);
  or or_1 (orAB, A, B);
  nand nand_1 (nandAB, A, B);
  nor nor_1 (norAB, A, B);
  xor xor_1 (xorAB, A, B);
  xor xor_2 (xor_2_out, A, B);
  xor xor_3 (xor3ABC, A, B, C);
  nand nand_2 (nand3ABC, A, B, C);
  nand nand_3 (nand_3_out, A, B);
  not not_2 (xnorAB, xor_2_out);
  nand nand_4 (CHAIN, nand_3_out, C);

  // Notes on the sheet:
  //   X
endmodule

module TN2 (
  input  x,
  input  y,
  input  z,
  output EQ1,
  output EQ2,
  output EQ3,
  output EQ4,
  output EQ5
);

  wire and_1_out, and_2_out, and_3_out, and_4_out, and_5_out, not_1_out, not_2_out, not_3_out, not_4_out,
       or_1_out, or_2_out, or_3_out, or_4_out, or_5_out, or_6_out, xor_1_out, xor_2_out, xor_3_out,
       xor_4_out, xor_5_out;

  not not_1 (not_1_out, x);
  not not_2 (not_2_out, y);
  or or_1 (or_1_out, x, y);
  and and_1 (and_1_out, not_1_out, not_2_out);
  and and_2 (and_2_out, x, y);
  and and_3 (and_3_out, y, z);
  not not_3 (not_3_out, or_1_out);
  not not_4 (not_4_out, and_2_out);
  or or_2 (or_2_out, y, x);
  or or_3 (or_3_out, x, z);
  and and_4 (and_4_out, not_1_out, y);
  or or_4 (or_4_out, y, x);
  or or_5 (or_5_out, and_3_out, x);
  and and_5 (and_5_out, or_2_out, or_3_out);
  or or_6 (or_6_out, and_4_out, x);
  xor xor_1 (xor_1_out, not_3_out, and_1_out);
  not not_5 (EQ1, xor_1_out);
  xor xor_2 (xor_2_out, not_4_out, and_1_out);
  not not_6 (EQ2, xor_2_out);
  xor xor_3 (xor_3_out, or_5_out, and_5_out);
  not not_7 (EQ3, xor_3_out);
  xor xor_4 (xor_4_out, or_6_out, x);
  not not_8 (EQ4, xor_4_out);
  xor xor_5 (xor_5_out, or_6_out, or_4_out);
  not not_9 (EQ5, xor_5_out);
endmodule

module TN3 (
  input  A,
  input  B,
  input  C,
  input  D,
  output F
);

  wire and_1_out, and_2_out, and_3_out, and_4_out, and_5_out, and_6_out, not_1_out, not_2_out, not_3_out,
       not_4_out;

  not not_1 (not_1_out, A);
  not not_2 (not_2_out, B);
  not not_3 (not_3_out, C);
  not not_4 (not_4_out, D);
  and and_1 (and_1_out, not_1_out, not_2_out, C, not_4_out);
  and and_2 (and_2_out, not_1_out, not_2_out, C, D);
  and and_3 (and_3_out, not_1_out, B, not_3_out, D);
  and and_4 (and_4_out, not_1_out, B, C, D);
  and and_5 (and_5_out, A, not_2_out, C, D);
  and and_6 (and_6_out, A, B, not_3_out, D);
  or or_1 (F, and_1_out, and_2_out, and_3_out, and_4_out, and_5_out, and_6_out);
endmodule

module TN4 (
  input  A,
  input  B,
  input  C,
  input  D,
  output EQ1,
  output EQ2
);

  wire and_1_out, and_2_out, and_3_out, and_4_out, and_5_out, and_6_out, and_7_out, and_8_out, and_9_out,
       and_10_out, and_11_out, F_sop_out, not_1_out, not_2_out, not_3_out, not_4_out, or_1_out, or_2_out,
       or_3_out, or_4_out, or_5_out, or_6_out, xor_1_out, xor_2_out;

  not not_1 (not_1_out, A);
  not not_2 (not_2_out, B);
  not not_3 (not_3_out, C);
  not not_4 (not_4_out, D);
  or or_1 (or_1_out, C, D);
  or or_2 (or_2_out, B, C);
  or or_3 (or_3_out, not_1_out, D);
  or or_4 (or_4_out, not_2_out, D);
  and and_1 (and_1_out, not_1_out, not_2_out, C, not_4_out);
  and and_2 (and_2_out, not_1_out, not_2_out, C, D);
  and and_3 (and_3_out, not_1_out, B, not_3_out, D);
  and and_4 (and_4_out, not_1_out, B, C, D);
  and and_5 (and_5_out, A, not_2_out, C, D);
  and and_6 (and_6_out, A, B, not_3_out, D);
  and and_7 (and_7_out, not_1_out, not_2_out, C);
  and and_8 (and_8_out, not_1_out, B, D);
  and and_9 (and_9_out, B, not_3_out, D);
  and and_10 (and_10_out, not_2_out, C, D);
  or or_5 (or_5_out, not_1_out, not_2_out, not_3_out);
  or or_6 (or_6_out, and_1_out, and_2_out, and_3_out, and_4_out, and_5_out, and_6_out);
  or F_sop (F_sop_out, and_7_out, and_8_out, and_9_out, and_10_out);
  and and_11 (and_11_out, or_1_out, or_2_out, or_3_out, or_4_out, or_5_out);
  not not_5 (EQ1, xor_1_out);
  xor xor_1 (xor_1_out, or_6_out, F_sop_out);
  not not_6 (EQ2, xor_2_out);
  xor xor_2 (xor_2_out, or_6_out, and_11_out);

  // Notes on the sheet:
  //   F_pos
  //   F_can
endmodule

module TN5 (
  input  A,
  input  B,
  input  C,
  output F
);

  wire xor_1_out;

  xor xor_1 (xor_1_out, A, B);
  xor xor_2 (F, xor_1_out, C);
endmodule
