// Logisim project IT012_lab02__25521955.circ as structural Verilog
module Warmup (
  input  [7:0] A,
  input  [7:0] B,
  output [7:0] out_3
);

  // Probe on A
  // Probe on B
  Adder adder_1 (.a(A), .b(B), .out(out_3));  // open: cin, cout
  // Probe on out_3
  // Probe on out_3
  // Probe on out_3
endmodule

module FA (
  input  A,
  input  B,
  input  Cin,
  output S,
  output Cout
);

  wire and_1_out, and_2_out, and_3_out, xor_1_out;

  xor xor_1 (xor_1_out, A, B);
  and and_1 (and_1_out, Cin, A);
  and and_2 (and_2_out, Cin, B);
  and and_3 (and_3_out, B, A);
  xor xor_2 (S, xor_1_out, Cin);
  or or_1 (Cout, and_1_out, and_2_out, and_3_out);
endmodule

module ADDSUB4 (
  input  [3:0] A,
  input  [3:0] B,
  input  [3:0] Sub,
  output C,
  output [3:0] S
);

  wire fa_1_cout, fa_2_cout, fa_3_cout, xor_1_out, xor_2_out, xor_3_out, xor_4_out;

  xor xor_1 (xor_1_out, B[0], Sub[0]);
  FA fa_1 (.A(A[0]), .B(xor_1_out), .Cin(Sub[0]), .S(S[0]), .Cout(fa_1_cout));
  xor xor_2 (xor_2_out, B[1], Sub[0]);
  // Probe on fa_1_cout
  FA fa_2 (.A(A[1]), .B(xor_2_out), .Cin(fa_1_cout), .S(S[1]), .Cout(fa_2_cout));
  // Probe on fa_2_cout
  xor xor_3 (xor_3_out, B[2], Sub[0]);
  FA fa_3 (.A(A[2]), .B(xor_3_out), .Cin(fa_2_cout), .S(S[2]), .Cout(fa_3_cout));
  xor xor_4 (xor_4_out, B[3], Sub[0]);
  // Probe on fa_3_cout
  FA fa_4 (.A(A[3]), .B(xor_4_out), .Cin(fa_3_cout), .S(S[3]), .Cout(C));
endmodule

module ALU8 (
  input  [2:0] in_1,
  input  [7:0] A,
  input  [7:0] B,
  output Z,
  output [7:0] R,
  output L
);

  wire [7:0] adder_1_out, adder_2_out, and_1_out, multiplexer_1_out, multiplexer_2_out, not_1_out, or_1_out,
       subtractor_1_out, subtractor_2_out, xor_1_out;

  Adder adder_1 (.a(A), .b(B), .out(adder_1_out));  // open: cin, cout
  Adder adder_2 (.a(A), .b(8'h1), .out(adder_2_out));  // open: cin, cout
  Subtractor subtractor_1 (.a(A), .b(B), .out(subtractor_1_out));  // open: bin, bout
  Subtractor subtractor_2 (.a(A), .b(8'h1), .out(subtractor_2_out));  // open: bin, bout
  assign and_1_out = A & B;  // AND_Gate and_1, 8 bits wide
  assign or_1_out = A | B;  // OR_Gate or_1, 8 bits wide
  assign not_1_out = ~A;  // NOT_Gate not_1, 8 bits wide
  assign xor_1_out = A ^ B;  // XOR_Gate xor_1, 8 bits wide
  Multiplexer #(.select(2), .width(8)) multiplexer_1 (
    .in0(adder_1_out), .in1(adder_2_out), .in2(subtractor_1_out), .in3(subtractor_2_out),
    .out(multiplexer_1_out), .sel(in_1[1:0]));
  Multiplexer #(.select(2), .width(8)) multiplexer_2 (
    .in0(and_1_out), .in1(or_1_out), .in2(not_1_out), .in3(xor_1_out), .out(multiplexer_2_out));  // open: sel
  LT lt_1 (.A7(A[7]), .B7(B[7]), .R7(R[7]), .out_4(L));
  Multiplexer #(.width(8)) multiplexer_3 (.in0(multiplexer_1_out), .in1(multiplexer_2_out), .out(R), .sel(in_1[2]));
  nor nor_1 (Z, R[0], R[1], R[2], R[3], R[4], R[5], R[6], R[7]);
endmodule

module LT (
  input  A7,
  input  B7,
  input  R7,
  output out_4
);

  wire and_1_out, and_2_out, and_3_out, not_1_out;

  not not_1 (not_1_out, B7);
  and and_1 (and_1_out, A7, not_1_out);
  and and_2 (and_2_out, not_1_out, R7);
  and and_3 (and_3_out, A7, R7);
  or or_1 (out_4, and_1_out, and_2_out, and_3_out);
endmodule

module TN3 (
  input  D,
  input  CLK,
  output Q2,
  output QQ2,
  output QQ1,
  output Q1
);

  D_Flip_Flop d_ff_1 (.D(D), .clk(CLK), .Q(Q2));  // open: Qn, preset, reset
  D_Flip_Flop d_ff_2 (.D(Q2), .clk(CLK), .Q(QQ2));  // open: Qn, preset, reset
  DLATCH latch1 (.E(CLK), .D(D), .Q(Q1));
  DLATCH latch2 (.E(CLK), .D(Q1), .Q(QQ1));
endmodule

module DLATCH (
  input  E,
  input  D,
  output Q
);

  Multiplexer multiplexer_1 (.in0(Q), .in1(D), .out(Q), .sel(E));
endmodule

module REGFILE (
  input  [1:0] RA,
  input  [1:0] RD,
  input  WE,
  input  [7:0] DIN,
  input  CLK,
  input  [1:0] RB,
  output [7:0] R0,
  output [7:0] QA,
  output [7:0] R1,
  output [7:0] R2,
  output [7:0] QB,
  output [7:0] R3
);

  wire decoder_1_out0, decoder_1_out1, decoder_1_out2, decoder_1_out3;

  Decoder #(.select(2)) decoder_1 (
    .out0(decoder_1_out0), .out1(decoder_1_out1), .out2(decoder_1_out2), .out3(decoder_1_out3), .sel(RD),
    .en(WE));
  Register register_1 (.D(DIN), .en(decoder_1_out0), .clk(CLK), .Q(R0));  // open: clr
  Register register_2 (.D(DIN), .en(decoder_1_out1), .clk(CLK), .Q(R1));  // open: clr
  Register register_3 (.D(DIN), .en(decoder_1_out2), .clk(CLK), .Q(R2));  // open: clr
  Register register_4 (.D(DIN), .en(decoder_1_out3), .clk(CLK), .Q(R3));  // open: clr
  Multiplexer #(.select(2), .width(8)) multiplexer_1 (.in0(R0), .in1(R1), .in2(R2), .in3(R3), .out(QA), .sel(RA));
  Multiplexer #(.select(2), .width(8)) multiplexer_2 (.in0(R0), .in1(R1), .in2(R2), .in3(R3), .out(QB), .sel(RB));
endmodule

module DATAPATH (
  input  [2:0] OOP,
  input  [1:0] RA,
  input  [1:0] RD,
  input  WE,
  input  CLK,
  input  [1:0] RB,
  input  [7:0] IMM,
  input  SRC,
  output Z,
  output [7:0] R0,
  output [7:0] R1,
  output [7:0] R2,
  output [7:0] R3
);

  wire [7:0] alu8_1_r, multiplexer_1_out, regfile_1_qa, regfile_1_qb;

  REGFILE regfile_1 (
    .RA(RA), .RD(RD), .WE(WE), .DIN(multiplexer_1_out), .CLK(CLK), .RB(RB), .R0(R0), .QA(regfile_1_qa),
    .R1(R1), .R2(R2), .QB(regfile_1_qb), .R3(R3));
  ALU8 alu8_1 (.in_1(OOP), .A(regfile_1_qa), .B(regfile_1_qb), .Z(Z), .R(alu8_1_r));  // open: L
  Multiplexer #(.width(8)) multiplexer_1 (.in0(alu8_1_r), .in1(IMM), .out(multiplexer_1_out), .sel(SRC));
endmodule
